// Logisim project Project1-Evolution.circ as structural Verilog: 5 circuits, main circuit main
module main (
);

  wire clock_1_out, clock_2_out, decimal_counter_1_l0, decimal_counter_1_l1, decimal_counter_1_l2,
       decimal_counter_1_l3, hex_logic_1_a, hex_logic_1_b, hex_logic_1_c, hex_logic_1_d, hex_logic_1_e,
       hex_logic_1_f, hex_logic_1_g, hexademical_counter_1_l0, hexademical_counter_1_l1,
       hexademical_counter_1_l2, hexademical_counter_1_l3, logic_1_a, logic_1_b, logic_1_c, logic_1_d,
       logic_1_e, logic_1_f, logic_1_g;

  Clock clock_1 (.out(clock_1_out));
  Clock clock_2 (.out(clock_2_out));
  hexademical_counter hexademical_counter_1 (
    .Clock(clock_1_out), .L0(hexademical_counter_1_l0), .L1(hexademical_counter_1_l1),
    .L2(hexademical_counter_1_l2), .L3(hexademical_counter_1_l3));  // open: IS_FIFTEEN
  decimal_counter decimal_counter_1 (
    .Clock(clock_2_out), .L3(decimal_counter_1_l3), .L2(decimal_counter_1_l2), .L1(decimal_counter_1_l1),
    .L0(decimal_counter_1_l0));  // open: IS_NINE
  hex_logic hex_logic_1 (
    .w(hexademical_counter_1_l0), .x(hexademical_counter_1_l1), .y(hexademical_counter_1_l2),
    .z(hexademical_counter_1_l3), .a(hex_logic_1_a), .b(hex_logic_1_b), .c(hex_logic_1_c), .d(hex_logic_1_d),
    .e(hex_logic_1_e), .f(hex_logic_1_f), .g(hex_logic_1_g));
  _7_Segment_Display u_7_segment_display_1 (
    .g(hex_logic_1_g), .f(hex_logic_1_f), .a(hex_logic_1_a), .b(hex_logic_1_b), .e(hex_logic_1_e),
    .d(hex_logic_1_d), .c(hex_logic_1_c));  // open: dp
  \logic  logic_1 (
    .w(decimal_counter_1_l3), .x(decimal_counter_1_l2), .y(decimal_counter_1_l1), .z(decimal_counter_1_l0),
    .a(logic_1_a), .b(logic_1_b), .c(logic_1_c), .d(logic_1_d), .e(logic_1_e), .f(logic_1_f), .g(logic_1_g));
  _7_Segment_Display u_7_segment_display_2 (
    .g(logic_1_g), .f(logic_1_f), .a(logic_1_a), .b(logic_1_b), .e(logic_1_e), .d(logic_1_d), .c(logic_1_c));  // open: dp
endmodule

module \logic  (
  input  w,
  input  x,
  input  y,
  input  z,
  output a,
  output b,
  output c,
  output d,
  output e,
  output f,
  output g
);

  wire and_1_out, and_2_out, and_3_out, and_4_out, nand_1_out, nand_2_out, nand_3_out, nor_1_out, not_1_out,
       not_2_out, not_3_out, not_4_out, not_5_out, or_1_out, or_2_out, or_3_out, or_5_out, xnor_1_out,
       xor_1_out;

  and and_1 (and_1_out, x, z);
  not not_1 (not_1_out, w);
  nand nand_1 (nand_1_out, x, z);
  or or_1 (or_1_out, x, z);
  not not_2 (not_2_out, y);
  nand nand_2 (nand_2_out, y, z);
  or or_2 (or_2_out, y, z);
  or or_3 (or_3_out, y, z, x);
  xnor xnor_1 (xnor_1_out, y, and_1_out);
  not not_3 (not_3_out, y);
  and and_2 (and_2_out, x, nand_3_out);
  nand nand_3 (nand_3_out, y, z);
  nor nor_1 (nor_1_out, z, y);
  not not_4 (not_4_out, z);
  and and_3 (and_3_out, not_4_out, y);
  xor xor_1 (xor_1_out, y, x);
  nand nand_4 (a, not_1_out, nand_1_out, or_1_out, not_2_out);
  nand nand_5 (b, x, nand_2_out, or_2_out);
  not not_5 (not_5_out, y);
  or or_4 (c, x, not_5_out, z);
  nand nand_6 (d, or_3_out, or_5_out);
  or or_5 (or_5_out, w, xnor_1_out);
  nor nor_2 (e, z, and_4_out);
  and and_4 (and_4_out, x, not_3_out);
  or or_6 (f, w, and_2_out, nor_1_out);
  or or_7 (g, w, and_3_out, xor_1_out);
endmodule

module decimal_counter (
  input  Clock,
  output L3,
  output L2,
  output L1,
  output L0,
  output IS_NINE
);

  wire and_1_out, and_2_out, and_3_out, and_4_out, and_5_out, and_6_out, and_7_out, d_ff_1_qn, d_ff_2_qn,
       d_ff_3_qn, d_ff_4_qn, or_1_out, or_2_out, or_3_out;

  and and_1 (and_1_out, L3, d_ff_4_qn);
  and and_2 (and_2_out, L2, L1, L0);
  and and_3 (and_3_out, L2, d_ff_3_qn);
  and and_4 (and_4_out, L2, d_ff_4_qn);
  and and_5 (and_5_out, d_ff_2_qn, L1, L0);
  and and_6 (and_6_out, L1, d_ff_4_qn);
  and and_7 (and_7_out, d_ff_1_qn, d_ff_3_qn, L0);
  and and_8 (IS_NINE, L3, d_ff_2_qn, d_ff_3_qn, L0);
  D_Flip_Flop d_ff_1 (.D(or_1_out), .clk(Clock), .Q(L3), .Qn(d_ff_1_qn));  // open: preset, reset
  or or_1 (or_1_out, and_1_out, and_2_out);
  D_Flip_Flop d_ff_2 (.D(or_2_out), .clk(Clock), .Q(L2), .Qn(d_ff_2_qn));  // open: preset, reset
  or or_2 (or_2_out, and_3_out, and_4_out, and_5_out);
  D_Flip_Flop d_ff_3 (.D(or_3_out), .clk(Clock), .Q(L1), .Qn(d_ff_3_qn));  // open: preset, reset
  or or_3 (or_3_out, and_6_out, and_7_out);
  D_Flip_Flop d_ff_4 (.D(d_ff_4_qn), .clk(Clock), .Q(L0), .Qn(d_ff_4_qn));  // open: preset, reset
endmodule

module hexademical_counter (
  input  Clock,
  output L0,
  output L1,
  output L2,
  output L3,
  output IS_FIFTEEN
);

  wire and_2_out, and_3_out, and_4_out, and_5_out, and_6_out, and_7_out, and_8_out, and_9_out, and_10_out,
       D1_qn, D2_qn, D3_qn, D4_qn, or_1_out, or_2_out, or_3_out;

  and and_1 (IS_FIFTEEN, L0, L1, L2, L3);
  and and_2 (and_2_out, L0, D2_qn);
  and and_3 (and_3_out, L0, D3_qn);
  and and_4 (and_4_out, L0, D4_qn);
  and and_5 (and_5_out, D1_qn, L1, L2, L3);
  and and_6 (and_6_out, L1, D3_qn);
  and and_7 (and_7_out, L1, D4_qn);
  and and_8 (and_8_out, D2_qn, L2, L3);
  and and_9 (and_9_out, L2, D4_qn);
  and and_10 (and_10_out, D3_qn, L3);
  D_Flip_Flop #(.trigger("falling")) D1 (.D(or_1_out), .clk(Clock), .Q(L0), .Qn(D1_qn));  // open: preset, reset
  or or_1 (or_1_out, and_2_out, and_3_out, and_4_out, and_5_out);
  D_Flip_Flop #(.trigger("falling")) D2 (.D(or_2_out), .clk(Clock), .Q(L1), .Qn(D2_qn));  // open: preset, reset
  or or_2 (or_2_out, and_6_out, and_7_out, and_8_out);
  D_Flip_Flop #(.trigger("falling")) D3 (.D(or_3_out), .clk(Clock), .Q(L2), .Qn(D3_qn));  // open: preset, reset
  or or_3 (or_3_out, and_9_out, and_10_out);
  D_Flip_Flop #(.trigger("falling")) D4 (.D(D4_qn), .clk(Clock), .Q(L3), .Qn(D4_qn));  // open: preset, reset
endmodule

module hex_logic (
  input  w,
  input  x,
  input  y,
  input  z,
  output a,
  output b,
  output c,
  output d,
  output e,
  output f,
  output g
);

  wire and_1_out, and_2_out, and_3_out, and_4_out, and_5_out, and_6_out, and_7_out, and_8_out, and_9_out,
       and_10_out, and_11_out, and_12_out, and_13_out, and_14_out, and_15_out, and_16_out, and_17_out,
       and_18_out, and_19_out, and_20_out, and_21_out, and_22_out, and_23_out, and_24_out, and_25_out,
       and_26_out, and_27_out, and_28_out, and_29_out, and_30_out, and_31_out, and_32_out, and_33_out,
       and_34_out, and_35_out, not_1_out, not_2_out, not_3_out, not_4_out;

  not not_1 (not_1_out, w);
  not not_2 (not_2_out, x);
  not not_3 (not_3_out, y);
  not not_4 (not_4_out, z);
  and and_1 (and_1_out, not_2_out, not_4_out);
  and and_2 (and_2_out, not_1_out, y);
  and and_3 (and_3_out, x, y);
  and and_4 (and_4_out, w, not_4_out);
  and and_5 (and_5_out, not_1_out, x, z);
  and and_6 (and_6_out, w, not_2_out, not_3_out);
  and and_7 (and_7_out, not_1_out, not_2_out);
  and and_8 (and_8_out, not_2_out, not_4_out);
  and and_9 (and_9_out, not_1_out, not_3_out, not_4_out);
  and and_10 (and_10_out, not_1_out, y, z);
  and and_11 (and_11_out, w, not_3_out, z);
  and and_12 (and_12_out, not_1_out, not_3_out);
  and and_13 (and_13_out, not_1_out, z);
  and and_14 (and_14_out, not_1_out, x);
  and and_15 (and_15_out, not_3_out, z);
  and and_16 (and_16_out, w, not_2_out);
  and and_17 (and_17_out, w, not_3_out);
  and and_18 (and_18_out, not_1_out, not_2_out, not_4_out);
  and and_19 (and_19_out, not_2_out, y, z);
  and and_20 (and_20_out, x, not_3_out, z);
  and and_21 (and_21_out, x, y, not_4_out);
  and and_22 (and_22_out, w, x);
  and and_23 (and_23_out, w, y);
  and and_24 (and_24_out, not_2_out, not_4_out);
  and and_25 (and_25_out, y, not_4_out);
  and and_26 (and_26_out, w, not_2_out);
  and and_27 (and_27_out, w, y);
  and and_28 (and_28_out, x, not_4_out);
  and and_29 (and_29_out, not_3_out, not_4_out);
  and and_30 (and_30_out, not_1_out, x, not_3_out);
  and and_31 (and_31_out, w, z);
  and and_32 (and_32_out, w, not_2_out);
  and and_33 (and_33_out, not_2_out, y);
  and and_34 (and_34_out, y, not_4_out);
  and and_35 (and_35_out, not_1_out, x, not_3_out);
  or or_1 (a, and_1_out, and_2_out, and_3_out, and_4_out, and_5_out, and_6_out);
  or or_2 (b, and_7_out, and_8_out, and_9_out, and_10_out, and_11_out);
  or or_3 (c, and_12_out, and_13_out, and_14_out, and_15_out, and_16_out);
  or or_4 (d, and_17_out, and_18_out, and_19_out, and_20_out, and_21_out);
  or or_5 (e, and_22_out, and_23_out, and_24_out, and_25_out);
  or or_6 (f, and_26_out, and_27_out, and_28_out, and_29_out, and_30_out);
  or or_7 (g, and_31_out, and_32_out, and_33_out, and_34_out, and_35_out);
endmodule
